// Logisim project logisim.circ as structural Verilog: 1 circuit, main circuit main
module main (
);

  // OR_Gate or_1 is placed but not wired
  // NOT_Gate not_1 is placed but not wired
  // AND_Gate and_1 is placed but not wired
endmodule
